# Fritzing sketch SchemaConnessioni (saved by Fritzing 0.9.9b)
breadboards: 1

parts:
  J1 = STM32 Nucleo boards
  microSD = MicroSD Card Module
  RTC_ds3231 = ZS-042 RTC Module
  Accelerometer_MPU6050 = InvenSense MPU6050
  Accelerometer_MPU6050_2 = InvenSense MPU6050

nets:
  N1: J1.D10_PWM/SS, microSD.CS
  N2: J1.D11_PWM/MOSI, microSD.MOSI
  N3: J1.D12/MISO, microSD.MISO
  N4: J1.D13/SCK, microSD.SCK
  N5: J1.A5/SCL, RTC_ds3231.SCL
  N6: J1.D7, Accelerometer_MPU6050.SCL, Accelerometer_MPU6050_2.SCL
  VCC: J1.3V3, Accelerometer_MPU6050.VCC, Accelerometer_MPU6050_2.VCC
  VCC_2: J1.5V, microSD.VCC, RTC_ds3231.VCC, Accelerometer_MPU6050_2.AD0
  GND: J1.GND#1188, Accelerometer_MPU6050.GND, Accelerometer_MPU6050_2.GND
  GND_2: J1.GND#1189, microSD.GND, RTC_ds3231.GND
  N7: J1.PC9, Accelerometer_MPU6050.SDA, Accelerometer_MPU6050_2.SDA
  N8: J1.PB7, RTC_ds3231.SDA
